# Fritzing sketch alubot (saved by Fritzing 0.9.3b)
breadboards: 1

parts:
  hc-sr1 = hc-sr04
  J1 = Basic Servo
  J2 = Basic Servo
  IR1 = TSOP312.., 314.. [package=THT]
  Composant1 = Arduino Uno (Rev3) - ICSP

nets:
  VCC: hc-sr1.VCC, J1.vcc, J2.vcc, IR1.Vs, Composant1.5V
  N1: hc-sr1.Trig, Composant1.D5_PWM
  N2: hc-sr1.Echo, Composant1.D4
  GND: hc-sr1.GND, J1.gnd, J2.gnd, IR1.GND, Composant1.GND
  N3: J1.pulse, Composant1.D3_PWM
  N4: J2.pulse, Composant1.D2
  N5: IR1.Data, Composant1.D11_PWM/MOSI
